// Logisim project 2-23-2023.circ as structural Verilog: 1 circuit, main circuit main
module main (
  input  in_1,
  input  in_2,
  input  in_3,
  input  in_4,
  output out_5
);

  wire and_1_out, and_2_out, and_3_out;

  and and_1 (and_1_out, ~in_2, ~in_3, in_4);  // AND_Gate
  and and_2 (and_2_out, in_1, in_2, in_3);
  and and_3 (and_3_out, ~in_1, ~in_3);  // AND_Gate
  or or_1 (out_5, and_1_out, and_2_out, and_3_out);
endmodule
