// Logisim project 2-28-2023.circ as structural Verilog: 1 circuit, main circuit main
module main (
  input  in_1,
  input  in_2,
  input  in_3,
  output out_4,
  output out_5,
  output out_6,
  output out_7
);

  wire and_1_out, and_2_out, or_1_out, xor_1_out;

  and and_1 (and_1_out, ~in_2, ~in_2, ~in_2);  // AND_Gate
  and and_2 (and_2_out, in_2, ~in_2, ~in_2);  // AND_Gate
  xor xor_1 (xor_1_out, in_2, in_2);
  or or_1 (or_1_out, and_1_out, and_1_out, and_2_out);
  D_Flip_Flop d_ff_1 (.clk(in_1), .D(xor_1_out), .Q(in_2));  // open: Qn, preset, en, reset
  D_Flip_Flop d_ff_2 (.clk(in_1), .D(or_1_out), .Q(in_2));  // open: Qn, preset, en, reset
  and and_3 (out_5, in_2, in_2);
  not not_1 (out_6, in_2);
  and and_4 (out_7, in_2, in_2);

  assign in_3 = in_2;
  assign out_4 = in_2;
endmodule
